// Logisim project Guia_05.circ as structural Verilog: 6 circuits, main circuit Exemplo_0501
module Exemplo_0501 (
  input  a,
  input  b,
  output s
);

  wire nand_1_out, nand_2_out, nand_3_out;

  nand nand_1 (nand_1_out, a, a);
  nand nand_2 (nand_2_out, b, b);
  nand nand_3 (nand_3_out, nand_1_out, nand_2_out);
  nand nand_4 (s, nand_3_out, nand_3_out);

  // Notes on the sheet:
  //   (a'.b')'
  //   a'
  //   b'
  //   a'.b'
endmodule

module Exemplo_0502 (
  input  a,
  input  b,
  output s
);

  wire nor_1_out, nor_2_out;

  nor nor_1 (nor_1_out, a, a);
  nor nor_2 (nor_2_out, nor_1_out, b);
  nor nor_3 (s, nor_2_out, nor_2_out);

  // Notes on the sheet:
  //   a'
  //   (a'+b)'
  //   a'+b
endmodule

module Exemplo_0503 (
  input  a,
  input  b,
  output s
);

  wire nand_1_out;

  nand nand_1 (nand_1_out, a, a);
  nand nand_2 (s, nand_1_out, b);

  // Notes on the sheet:
  //   a'
  //   (a'.b)'=(a+b')
  //   b
endmodule

module Exemplo_0504 (
  input  a,
  input  b,
  output s
);

  wire nor_1_out;

  nor nor_1 (nor_1_out, b, b);
  nor nor_2 (s, a, nor_1_out);

  // Notes on the sheet:
  //   a
  //   b'
  //   (a+b')'=(a'.b)
endmodule

module Exemplo_0505 (
  input  a,
  input  b,
  output s
);

  wire nand_1_out, nand_2_out, nand_3_out, nand_4_out;

  nand nand_1 (nand_1_out, a, b);
  nand nand_2 (nand_2_out, a, nand_1_out);
  nand nand_3 (nand_3_out, nand_2_out, nand_4_out);
  nand nand_4 (nand_4_out, nand_1_out, b);
  nand nand_5 (s, nand_3_out, nand_3_out);

  // Notes on the sheet:
  //   w1=(a.b)'
  //   a
  //   b
  //   w2=((a.b)'.a)'
  //   w3=((a.b)'.b)'
  //   w4=(a xor b)
  //   s=a xnor b
endmodule

module Exemplo_0506 (
  input  a,
  input  b,
  output s
);

  wire nor_1_out, nor_2_out, nor_3_out, nor_4_out;

  nor nor_1 (nor_1_out, a, b);
  nor nor_2 (nor_2_out, a, nor_1_out);
  nor nor_3 (nor_3_out, nor_2_out, nor_4_out);
  nor nor_4 (nor_4_out, nor_1_out, b);
  nor nor_5 (s, nor_3_out, nor_3_out);

  // Notes on the sheet:
  //   w1=(a+b)'
  //   a
  //   b
  //   w2=((a+b)'+a)'
  //   w4=a xnor b
  //   w3=((a+b)'+b)'
  //   s=a xor b
endmodule
