// Logisim project Guia_07.circ as structural Verilog: 5 circuits, main circuit 0701
module _0701 (
  input  a,
  input  b,
  input  select,
  output s
);

  wire and_2_out, and_3_out, AND_out, NAND_out, not_1_out;

  and AND (AND_out, a, b);
  nand NAND (NAND_out, a, b);
  not not_1 (not_1_out, select);
  and and_2 (and_2_out, AND_out, not_1_out);
  and and_3 (and_3_out, NAND_out, select);
  or or_1 (s, and_2_out, and_3_out);

  // Notes on the sheet:
  //   s1
  //   s2
  //   0 - AND$1 - NAND
endmodule

module _0702 (
  input  a,
  input  b,
  input  select,
  output s
);

  wire and_1_out, and_2_out, NOR_out, not_1_out, OR_out;

  or OR (OR_out, a, b);
  nor NOR (NOR_out, a, b);
  not not_1 (not_1_out, select);
  and and_1 (and_1_out, OR_out, not_1_out);
  and and_2 (and_2_out, NOR_out, select);
  or or_2 (s, and_1_out, and_2_out);

  // Notes on the sheet:
  //   s1
  //   s2
  //   0 - OR$1 - NOR
endmodule

module _0703 (
  input  a,
  input  b,
  input  select1,
  input  select2,
  output s
);

  wire and_2_out, and_3_out, and_4_out, and_5_out, and_6_out, and_7_out, AND_out, NAND_out, NOR_out,
       not_1_out, not_2_out, or_2_out, or_3_out, OR_out;

  and AND (AND_out, a, b);
  or OR (OR_out, a, b);
  nand NAND (NAND_out, a, b);
  nor NOR (NOR_out, a, b);
  not not_1 (not_1_out, select1);
  and and_2 (and_2_out, AND_out, not_1_out);
  and and_3 (and_3_out, NAND_out, select1);
  and and_4 (and_4_out, OR_out, not_1_out);
  and and_5 (and_5_out, NOR_out, select1);
  or or_2 (or_2_out, and_2_out, and_3_out);
  or or_3 (or_3_out, and_4_out, and_5_out);
  and and_6 (and_6_out, or_2_out, not_2_out);
  and and_7 (and_7_out, or_3_out, select2);
  not not_2 (not_2_out, select2);
  or or_4 (s, and_6_out, and_7_out);

  // Notes on the sheet:
  //   sA1
  //   sA2
  //   sB1
  //   sB2
  //   0 -  AND   / OR$1 - NAND / NOR
  //   sA
  //   sB
  //   0 - AND / NAND$1 -   OR / NOR
endmodule

module _0704 (
  input  a,
  input  b,
  input  select1,
  input  select2,
  output s
);

  wire and_1_out, and_2_out, and_3_out, and_4_out, and_5_out, and_6_out, NOR_out, not_1_out, not_2_out,
       or_2_out, or_3_out, OR_out, XNOR_out, XOR_out;

  xor XOR (XOR_out, a, b);
  or OR (OR_out, a, b);
  nor NOR (NOR_out, a, b);
  xnor XNOR (XNOR_out, a, b);
  not not_1 (not_1_out, select1);
  and and_1 (and_1_out, XOR_out, not_1_out);
  and and_2 (and_2_out, XNOR_out, select1);
  and and_3 (and_3_out, OR_out, not_1_out);
  and and_4 (and_4_out, NOR_out, select1);
  or or_2 (or_2_out, and_1_out, and_2_out);
  or or_3 (or_3_out, and_3_out, and_4_out);
  and and_5 (and_5_out, or_2_out, not_2_out);
  and and_6 (and_6_out, or_3_out, select2);
  not not_2 (not_2_out, select2);
  or or_4 (s, and_5_out, and_6_out);

  // Notes on the sheet:
  //   sA1
  //   sA2
  //   sB1
  //   sB2
  //   0 -  XOR   / OR$1 - XNOR / NOR
  //   sA
  //   sB
  //   0 - XOR / XNOR$1 -   OR / NOR
endmodule

module _0705 (
  input  a,
  input  b,
  input  in_3,
  input  in_4,
  input  in_5,
  output s
);

  wire AND_out, multiplexer_1_out, multiplexer_2_out, multiplexer_3_out, multiplexer_4_out,
       multiplexer_5_out, multiplexer_6_out, NAND_out, NOR_out, not_1_out, not_2_out, OR_out, XNOR_out,
       XOR_out;

  and AND (AND_out, a, b);
  or OR (OR_out, a, b);
  not not_1 (not_1_out, a);
  not not_2 (not_2_out, b);
  nand NAND (NAND_out, a, b);
  nor NOR (NOR_out, a, b);
  xor XOR (XOR_out, a, b);
  xnor XNOR (XNOR_out, a, b);
  Multiplexer #(.enable("false")) multiplexer_1 (.in0(AND_out), .in1(NAND_out), .out(multiplexer_1_out), .sel(in_3));
  Multiplexer #(.enable("false")) multiplexer_2 (.in0(OR_out), .in1(NOR_out), .out(multiplexer_2_out), .sel(in_3));
  Multiplexer #(.enable("false")) multiplexer_3 (.in0(XOR_out), .in1(XNOR_out), .out(multiplexer_3_out), .sel(in_3));
  Multiplexer #(.enable("false")) multiplexer_4 (.in0(not_1_out), .in1(not_2_out), .out(multiplexer_4_out), .sel(in_3));
  Multiplexer #(.enable("false")) multiplexer_5 (
    .in0(multiplexer_1_out), .in1(multiplexer_2_out), .out(multiplexer_5_out), .sel(in_4));
  Multiplexer #(.enable("false")) multiplexer_6 (
    .in0(multiplexer_3_out), .in1(multiplexer_4_out), .out(multiplexer_6_out), .sel(in_4));
  Multiplexer #(.enable("false")) multiplexer_7 (.in0(multiplexer_5_out), .in1(multiplexer_6_out), .out(s), .sel(in_5));

  // Notes on the sheet:
  //   sA1
  //   sA2
  //   sB1
  //   sB2
  //   sC1
  //   sC2
  //   sD1
  //   sD2
  //   sA
  //   sB
  //   sC
  //   sD
  //   s01
  //   s02
  //   000 - AND$001 - XOR$010 - OR$011 - NOT(a)$100 - NAND$101 - XNOR$110 - NOR$111 - NOT(b)
endmodule
