// Logisim project Guia_08.circ as structural Verilog: 11 circuits, main circuit HA
module HA (
  input  x,
  input  y,
  output s0,
  output s1
);

  xor xor_1 (s0, x, y);
  and and_1 (s1, y, x);
endmodule

module FA (
  input  carry_in,
  input  x,
  input  y,
  output s0,
  output s1_carry_out
);

  wire ha_1_s0, ha_1_s1, ha_2_s1;

  HA ha_1 (.x(carry_in), .y(x), .s0(ha_1_s0), .s1(ha_1_s1));
  HA ha_2 (.x(ha_1_s0), .y(y), .s0(s0), .s1(ha_2_s1));
  or or_1 (s1_carry_out, ha_2_s1, ha_1_s1);
endmodule

module FA2 (
  input  x1,
  input  x0,
  input  y1,
  input  y0,
  input  carry_in,
  output s1,
  output s01,
  output s00
);

  wire fa_2_s1_carry_out;

  FA fa_1 (.x(x1), .y(y1), .s0(s01), .s1_carry_out(s1), .carry_in(fa_2_s1_carry_out));
  FA fa_2 (.x(x0), .y(y0), .s0(s00), .s1_carry_out(fa_2_s1_carry_out), .carry_in(carry_in));
endmodule

module FA5 (
  input  x4,
  input  x3,
  input  x2,
  input  x1,
  input  x0,
  input  y4,
  input  y3,
  input  y2,
  input  y1,
  input  y0,
  input  carry_in,
  output s1,
  output s04,
  output s03,
  output s02,
  output s01,
  output s00
);

  wire fa2_1_s1, fa2_2_s1;

  FA fa_1 (.x(x4), .y(y4), .s0(s04), .s1_carry_out(s1), .carry_in(fa2_1_s1));
  FA2 fa2_1 (.s1(fa2_1_s1), .carry_in(fa2_2_s1), .y1(y3), .x1(x3), .y0(y2), .x0(x2), .s01(s03), .s00(s02));
  FA2 fa2_2 (.s1(fa2_2_s1), .carry_in(carry_in), .y1(y1), .x1(x1), .y0(y0), .x0(x0), .s01(s01), .s00(s00));
endmodule

module HS (
  input  x,
  input  y,
  output s0,
  output s1
);

  wire not_1_out;

  not not_1 (not_1_out, x);
  xor xor_1 (s0, x, y);
  and and_1 (s1, y, not_1_out);
endmodule

module FS (
  input  x,
  input  y,
  input  carry_in,
  output s0,
  output s1_carry_out
);

  wire hs_1_s0, hs_1_s1, hs_2_s1;

  HS hs_1 (.x(x), .y(y), .s0(hs_1_s0), .s1(hs_1_s1));
  HS hs_2 (.x(hs_1_s0), .y(carry_in), .s0(s0), .s1(hs_2_s1));
  or or_1 (s1_carry_out, hs_2_s1, hs_1_s1);
endmodule

module FS2 (
  input  x1,
  input  x0,
  input  y1,
  input  y0,
  input  carry_in,
  output s1,
  output s01,
  output s00
);

  wire fs_2_s1_carry_out;

  FS fs_1 (.y(y1), .carry_in(fs_2_s1_carry_out), .s0(s01), .s1_carry_out(s1), .x(x1));
  FS fs_2 (.y(y0), .carry_in(carry_in), .s0(s00), .s1_carry_out(fs_2_s1_carry_out), .x(x0));
endmodule

module FS5 (
  input  x4,
  input  x3,
  input  x2,
  input  x1,
  input  x0,
  input  y4,
  input  y3,
  input  y2,
  input  y1,
  input  y0,
  input  carry_in,
  output s1,
  output s04,
  output s03,
  output s02,
  output s01,
  output s00
);

  wire fs2_1_s1, fs2_2_s1;

  FS fs_1 (.y(y4), .carry_in(fs2_1_s1), .s0(s04), .s1_carry_out(s1), .x(x4));
  FS2 fs2_1 (.s1(fs2_1_s1), .carry_in(fs2_2_s1), .y1(y3), .x1(x3), .y0(y2), .x0(x2), .s01(s03), .s00(s02));
  FS2 fs2_2 (.s1(fs2_2_s1), .carry_in(carry_in), .y1(y1), .x1(x1), .y0(y0), .x0(x0), .s01(s01), .s00(s00));
endmodule

// =
module Igual (
  input  x,
  input  y,
  output s
);

  xnor xnor_1 (s, x, y);
endmodule

module Comparador (
  input  x4,
  input  x3,
  input  x2,
  input  x1,
  input  x0,
  input  y4,
  input  y3,
  input  y2,
  input  y1,
  input  y0,
  output s1_diferente,
  output s2_igual
);

  wire igual_1_s, igual_2_s, igual_3_s, igual_4_s, igual_5_s;

  Igual igual_1 (.x(x4), .y(y4), .s(igual_1_s));
  Igual igual_2 (.x(x2), .y(y2), .s(igual_2_s));
  Igual igual_3 (.x(x3), .y(y3), .s(igual_3_s));
  Igual igual_4 (.x(x0), .y(y0), .s(igual_4_s));
  Igual igual_5 (.x(x1), .y(y1), .s(igual_5_s));
  and and_1 (s2_igual, igual_4_s, igual_5_s, igual_2_s, igual_3_s, igual_1_s);
  not not_1 (s1_diferente, s2_igual);
endmodule

module C2_5 (
  input  x4,
  input  x3,
  input  x2,
  input  x1,
  input  x0,
  output out_6,
  output out_7,
  output out_8,
  output out_9,
  output out_10,
  output out_11
);

  wire ha_2_s1, ha_3_s1, ha_4_s1, ha_5_s1, not_1_out, not_2_out, not_3_out, not_4_out, not_5_out;

  not not_1 (not_1_out, x4);
  HA ha_1 (.x(ha_2_s1), .y(not_1_out), .s0(out_7), .s1(out_6));
  not not_2 (not_2_out, x3);
  HA ha_2 (.x(ha_3_s1), .y(not_2_out), .s0(out_8), .s1(ha_2_s1));
  not not_3 (not_3_out, x2);
  HA ha_3 (.x(ha_4_s1), .y(not_3_out), .s0(out_9), .s1(ha_3_s1));
  HA ha_4 (.x(ha_5_s1), .y(not_4_out), .s0(out_10), .s1(ha_4_s1));
  not not_4 (not_4_out, x1);
  HA ha_5 (.x(1'b1), .y(not_5_out), .s0(out_11), .s1(ha_5_s1));
  not not_5 (not_5_out, x0);
endmodule
