// Logisim project Guia_11.circ as structural Verilog: 2 circuits, main circuit Identify_110
module Identify_110 (
  input  in_1,
  input  in_2,
  output out_3
);

  wire clock_1_out, d_ff_1_q, d_ff_1_qn, d_ff_2_q, d_ff_3_q;

  Clock clock_1 (.out(clock_1_out));
  D_Flip_Flop d_ff_1 (.clk(clock_1_out), .D(in_1), .Q(d_ff_1_q), .Qn(d_ff_1_qn), .reset(in_2));  // open: preset
  D_Flip_Flop d_ff_2 (.clk(clock_1_out), .D(d_ff_1_q), .Q(d_ff_2_q), .reset(in_2));  // open: Qn, preset
  D_Flip_Flop d_ff_3 (.clk(clock_1_out), .D(d_ff_2_q), .Q(d_ff_3_q), .reset(in_2));  // open: Qn, preset
  and and_1 (out_3, d_ff_3_q, d_ff_2_q, d_ff_1_qn);
endmodule

module Identify_1101 (
  input  in_1,
  input  in_2,
  output out_3
);

  wire clock_1_out, d_ff_1_q, d_ff_2_q, d_ff_2_qn, d_ff_3_q, d_ff_4_q;

  Clock clock_1 (.out(clock_1_out));
  D_Flip_Flop d_ff_1 (.clk(clock_1_out), .D(in_1), .Q(d_ff_1_q), .reset(in_2));  // open: Qn, preset
  D_Flip_Flop d_ff_2 (.clk(clock_1_out), .D(d_ff_1_q), .Q(d_ff_2_q), .Qn(d_ff_2_qn), .reset(in_2));  // open: preset
  D_Flip_Flop d_ff_3 (.clk(clock_1_out), .D(d_ff_2_q), .Q(d_ff_3_q), .reset(in_2));  // open: Qn, preset
  D_Flip_Flop d_ff_4 (.clk(clock_1_out), .D(d_ff_3_q), .Q(d_ff_4_q), .reset(in_2));  // open: Qn, preset
  and and_1 (out_3, d_ff_4_q, d_ff_3_q, d_ff_2_qn, d_ff_1_q);
endmodule
