// Logisim project Guia_12.circ as structural Verilog: 8 circuits, main circuit RAM_1x4_a
// 1x1
module RAM_1x1 (
  input  address,
  input  R_W,
  input  CLK,
  input  \input ,
  input  CLR,
  output \output 
);

  wire and_1_out, j_k_ff_1_q, not_1_out;

  and and_1 (and_1_out, address, R_W, CLK);
  not not_1 (not_1_out, \input );
  and and_2 (\output , address, j_k_ff_1_q);
  J_K_Flip_Flop j_k_ff_1 (
    .J(\input ), .clk(and_1_out), .K(not_1_out), .Q(j_k_ff_1_q), .reset(CLR));  // open: Qn, preset
endmodule

// 1x2
module RAM_1x2 (
  input  R_W,
  input  address,
  input  CLK,
  input  CLR,
  input  [1:0] \input ,
  output [1:0] \output 
);

  RAM_1x1 ram_1x1_1 (.R_W(R_W), .CLK(CLK), .\input (\input [0]), .address(address), .\output (\output [0]), .CLR(CLR));
  RAM_1x1 ram_1x1_2 (.R_W(R_W), .CLK(CLK), .\input (\input [1]), .address(address), .\output (\output [1]), .CLR(CLR));
endmodule

module RAM_1x4_a (
  input  address,
  input  R_W,
  input  CLK,
  input  input_0,
  input  input_1,
  input  input_2,
  input  input_3,
  input  CLR,
  output output_0,
  output output_1,
  output output_2,
  output output_3
);

  wire and_1_out, j_k_ff_1_q, j_k_ff_2_q, j_k_ff_3_q, j_k_ff_4_q, not_1_out, not_2_out, not_3_out, not_4_out;

  and and_1 (and_1_out, address, R_W, CLK);
  not not_1 (not_1_out, input_0);
  not not_2 (not_2_out, input_1);
  not not_3 (not_3_out, input_2);
  not not_4 (not_4_out, input_3);
  J_K_Flip_Flop j_k_ff_1 (
    .J(input_0), .clk(and_1_out), .K(not_1_out), .Q(j_k_ff_1_q), .reset(CLR));  // open: Qn, preset
  J_K_Flip_Flop j_k_ff_2 (
    .J(input_1), .clk(and_1_out), .K(not_2_out), .Q(j_k_ff_2_q), .reset(CLR));  // open: Qn, preset
  J_K_Flip_Flop j_k_ff_3 (
    .J(input_2), .clk(and_1_out), .K(not_3_out), .Q(j_k_ff_3_q), .reset(CLR));  // open: Qn, preset
  J_K_Flip_Flop j_k_ff_4 (
    .J(input_3), .clk(and_1_out), .K(not_4_out), .Q(j_k_ff_4_q), .reset(CLR));  // open: Qn, preset
  and and_2 (output_0, address, j_k_ff_1_q);
  and and_3 (output_1, address, j_k_ff_2_q);
  and and_4 (output_2, address, j_k_ff_3_q);
  and and_5 (output_3, address, j_k_ff_4_q);
endmodule

// 1x4
module RAM_1x4_b (
  input  R_W,
  input  address,
  input  CLK,
  input  CLR,
  input  [3:0] \input ,
  output [3:0] \output 
);

  RAM_1x2 ram_1x2_1 (
    .R_W(R_W), .CLK(CLK), .CLR(CLR), .address(address), .\output (\output [1:0]), .\input (\input [1:0]));
  RAM_1x2 ram_1x2_2 (
    .R_W(R_W), .CLK(CLK), .CLR(CLR), .address(address), .\output (\output [3:2]), .\input (\input [3:2]));
endmodule

// 1x8
module RAM_1x8 (
  input  R_W,
  input  address,
  input  CLK,
  input  CLR,
  input  [7:0] \input ,
  output [7:0] \output 
);

  RAM_1x4_b ram_1x4_b_1 (
    .R_W(R_W), .CLK(CLK), .CLR(CLR), .address(address), .\output (\output [3:0]), .\input (\input [3:0]));
  RAM_1x4_b ram_1x4_b_2 (
    .R_W(R_W), .CLK(CLK), .CLR(CLR), .address(address), .\output (\output [7:4]), .\input (\input [7:4]));
endmodule

// 2x4
module RAM_2x4 (
  input  address,
  input  R_W,
  input  [3:0] \input ,
  input  CLK,
  input  CLR,
  output [3:0] \output 
);

  wire demultiplexer_1_out0, demultiplexer_1_out1;
  wire [3:0] ram_1x4_b_1_output, ram_1x4_b_2_output;

  Demultiplexer #(.enable("false")) demultiplexer_1 (
    .out0(demultiplexer_1_out0), .out1(demultiplexer_1_out1), .in(1'b1), .sel(address));
  RAM_1x4_b ram_1x4_b_1 (
    .R_W(R_W), .CLK(CLK), .CLR(CLR), .address(demultiplexer_1_out0), .\output (ram_1x4_b_1_output),
    .\input (\input ));
  RAM_1x4_b ram_1x4_b_2 (
    .R_W(R_W), .CLK(CLK), .CLR(CLR), .address(demultiplexer_1_out1), .\output (ram_1x4_b_2_output),
    .\input (\input ));
  Multiplexer #(.width(4), .enable("false")) multiplexer_1 (
    .in0(ram_1x4_b_1_output), .in1(ram_1x4_b_2_output), .out(\output ), .sel(address));
endmodule

// 4x8
module RAM_4x8 (
  input  [1:0] address,
  input  R_W,
  input  [7:0] \input ,
  input  CLK,
  input  CLR,
  output [7:0] \output 
);

  wire demultiplexer_1_out0, demultiplexer_1_out1, demultiplexer_1_out2, demultiplexer_1_out3;
  wire [7:0] ram_1x8_1_output, ram_1x8_2_output, ram_1x8_3_output, ram_1x8_4_output;

  Demultiplexer #(.select(2), .enable("false")) demultiplexer_1 (
    .out0(demultiplexer_1_out0), .out1(demultiplexer_1_out1), .out2(demultiplexer_1_out2),
    .out3(demultiplexer_1_out3), .in(1'b1), .sel(address));
  RAM_1x8 ram_1x8_1 (
    .R_W(R_W), .CLK(CLK), .CLR(CLR), .address(demultiplexer_1_out0), .\output (ram_1x8_1_output),
    .\input (\input ));
  RAM_1x8 ram_1x8_2 (
    .R_W(R_W), .CLK(CLK), .CLR(CLR), .address(demultiplexer_1_out1), .\output (ram_1x8_2_output),
    .\input (\input ));
  RAM_1x8 ram_1x8_3 (
    .R_W(R_W), .CLK(CLK), .CLR(CLR), .address(demultiplexer_1_out2), .\output (ram_1x8_3_output),
    .\input (\input ));
  RAM_1x8 ram_1x8_4 (
    .R_W(R_W), .CLK(CLK), .CLR(CLR), .address(demultiplexer_1_out3), .\output (ram_1x8_4_output),
    .\input (\input ));
  Multiplexer #(.select(2), .width(8), .enable("false")) multiplexer_1 (
    .in0(ram_1x8_1_output), .in1(ram_1x8_2_output), .in2(ram_1x8_3_output), .in3(ram_1x8_4_output),
    .out(\output ), .sel(address));
endmodule

module RAM_8x8 (
  input  [2:0] address,
  input  R_W,
  input  [7:0] \input ,
  input  CLK,
  input  CLR,
  output [7:0] \output 
);

  wire demultiplexer_1_out0, demultiplexer_1_out1, demultiplexer_1_out2, demultiplexer_1_out3,
       demultiplexer_1_out4, demultiplexer_1_out5, demultiplexer_1_out6, demultiplexer_1_out7;
  wire [7:0] ram_1x8_1_output, ram_1x8_2_output, ram_1x8_3_output, ram_1x8_4_output, ram_1x8_5_output,
       ram_1x8_6_output, ram_1x8_7_output, ram_1x8_8_output;

  Demultiplexer #(.select(3), .enable("false")) demultiplexer_1 (
    .out0(demultiplexer_1_out0), .out1(demultiplexer_1_out1), .out2(demultiplexer_1_out2),
    .out3(demultiplexer_1_out3), .out4(demultiplexer_1_out4), .out5(demultiplexer_1_out5),
    .out6(demultiplexer_1_out6), .out7(demultiplexer_1_out7), .in(1'b1), .sel(address));
  RAM_1x8 ram_1x8_1 (
    .R_W(R_W), .CLK(CLK), .CLR(CLR), .address(demultiplexer_1_out0), .\output (ram_1x8_1_output),
    .\input (\input ));
  RAM_1x8 ram_1x8_2 (
    .R_W(R_W), .CLK(CLK), .CLR(CLR), .address(demultiplexer_1_out1), .\output (ram_1x8_2_output),
    .\input (\input ));
  RAM_1x8 ram_1x8_3 (
    .R_W(R_W), .CLK(CLK), .CLR(CLR), .address(demultiplexer_1_out2), .\output (ram_1x8_3_output),
    .\input (\input ));
  RAM_1x8 ram_1x8_4 (
    .R_W(R_W), .CLK(CLK), .CLR(CLR), .address(demultiplexer_1_out3), .\output (ram_1x8_4_output),
    .\input (\input ));
  RAM_1x8 ram_1x8_5 (
    .R_W(R_W), .CLK(CLK), .CLR(CLR), .address(demultiplexer_1_out4), .\output (ram_1x8_5_output),
    .\input (\input ));
  RAM_1x8 ram_1x8_6 (
    .R_W(R_W), .CLK(CLK), .CLR(CLR), .address(demultiplexer_1_out5), .\output (ram_1x8_6_output),
    .\input (\input ));
  RAM_1x8 ram_1x8_7 (
    .R_W(R_W), .CLK(CLK), .CLR(CLR), .address(demultiplexer_1_out6), .\output (ram_1x8_7_output),
    .\input (\input ));
  RAM_1x8 ram_1x8_8 (
    .R_W(R_W), .CLK(CLK), .CLR(CLR), .address(demultiplexer_1_out7), .\output (ram_1x8_8_output),
    .\input (\input ));
  Multiplexer #(.select(3), .width(8), .enable("false")) multiplexer_1 (
    .in0(ram_1x8_1_output), .in1(ram_1x8_2_output), .in2(ram_1x8_3_output), .in3(ram_1x8_4_output),
    .in4(ram_1x8_5_output), .in5(ram_1x8_6_output), .in6(ram_1x8_7_output), .in7(ram_1x8_8_output),
    .out(\output ), .sel(address));
endmodule
