// Logisim project Guia_13.circ as structural Verilog: 5 circuits, main circuit decresc_as
module decresc_as (
  input  x,
  input  CLR
);

  wire CLK_out, j_k_ff_1_q, j_k_ff_2_q, j_k_ff_3_q, j_k_ff_4_q, j_k_ff_5_q, j_k_ff_6_q;

  Clock CLK (.out(CLK_out));
  J_K_Flip_Flop j_k_ff_1 (.J(x), .clk(CLK_out), .K(x), .Q(j_k_ff_1_q), .reset(CLR));  // open: Qn, preset
  // Probe on j_k_ff_6_q
  J_K_Flip_Flop j_k_ff_2 (.J(x), .clk(j_k_ff_1_q), .K(x), .Q(j_k_ff_2_q), .reset(CLR));  // open: Qn, preset
  // Probe on j_k_ff_4_q
  // Probe on j_k_ff_5_q
  J_K_Flip_Flop j_k_ff_3 (.J(x), .clk(j_k_ff_2_q), .K(x), .Q(j_k_ff_3_q), .reset(CLR));  // open: Qn, preset
  // Probe on j_k_ff_3_q
  J_K_Flip_Flop j_k_ff_4 (.J(x), .clk(j_k_ff_3_q), .K(x), .Q(j_k_ff_4_q), .reset(CLR));  // open: Qn, preset
  // Probe on j_k_ff_2_q
  J_K_Flip_Flop j_k_ff_5 (.J(x), .clk(j_k_ff_4_q), .K(x), .Q(j_k_ff_5_q), .reset(CLR));  // open: Qn, preset
  // Probe on j_k_ff_1_q
  J_K_Flip_Flop j_k_ff_6 (.J(x), .clk(j_k_ff_5_q), .K(x), .Q(j_k_ff_6_q), .reset(CLR));  // open: Qn, preset

  // Notes on the sheet:
  //   Contador assíncrono$decrescente (6 bits)
endmodule

module cresc_as (
  input  x,
  input  CLR
);

  wire CLK_out, j_k_ff_1_q, j_k_ff_1_qn, j_k_ff_2_q, j_k_ff_2_qn, j_k_ff_3_q, j_k_ff_3_qn, j_k_ff_4_q,
       j_k_ff_4_qn, j_k_ff_5_q, j_k_ff_5_qn, j_k_ff_6_q;

  Clock CLK (.out(CLK_out));
  J_K_Flip_Flop j_k_ff_1 (.J(x), .clk(CLK_out), .K(x), .Q(j_k_ff_1_q), .Qn(j_k_ff_1_qn), .reset(CLR));  // open: preset
  // Probe on j_k_ff_6_q
  // Probe on j_k_ff_5_q
  J_K_Flip_Flop j_k_ff_2 (
    .J(x), .clk(j_k_ff_1_qn), .K(x), .Q(j_k_ff_2_q), .Qn(j_k_ff_2_qn), .reset(CLR));  // open: preset
  // Probe on j_k_ff_4_q
  // Probe on j_k_ff_3_q
  J_K_Flip_Flop j_k_ff_3 (
    .J(x), .clk(j_k_ff_2_qn), .K(x), .Q(j_k_ff_3_q), .Qn(j_k_ff_3_qn), .reset(CLR));  // open: preset
  // Probe on j_k_ff_2_q
  // Probe on j_k_ff_1_q
  J_K_Flip_Flop j_k_ff_4 (
    .J(x), .clk(j_k_ff_3_qn), .K(x), .Q(j_k_ff_4_q), .Qn(j_k_ff_4_qn), .reset(CLR));  // open: preset
  J_K_Flip_Flop j_k_ff_5 (
    .J(x), .clk(j_k_ff_4_qn), .K(x), .Q(j_k_ff_5_q), .Qn(j_k_ff_5_qn), .reset(CLR));  // open: preset
  J_K_Flip_Flop j_k_ff_6 (.J(x), .clk(j_k_ff_5_qn), .K(x), .Q(j_k_ff_6_q), .reset(CLR));  // open: Qn, preset

  // Notes on the sheet:
  //   Contador assíncrono$crescente (6 bits)
endmodule

module dec_cresc_as (
  input  x,
  input  CLR
);

  wire and_1_out, CLK_out, j_k_ff_1_q, j_k_ff_1_qn, j_k_ff_2_q, j_k_ff_2_qn, j_k_ff_3_q, j_k_ff_3_qn,
       j_k_ff_4_q, j_k_ff_4_qn, j_k_ff_5_q, j_k_ff_5_qn, or_1_out;

  Clock CLK (.out(CLK_out));
  and and_1 (and_1_out, j_k_ff_1_qn, j_k_ff_2_q, j_k_ff_3_qn, j_k_ff_4_q, j_k_ff_5_qn);
  J_K_Flip_Flop j_k_ff_1 (
    .J(x), .clk(CLK_out), .K(x), .Q(j_k_ff_1_q), .Qn(j_k_ff_1_qn), .reset(or_1_out));  // open: preset
  or or_1 (or_1_out, CLR, and_1_out);
  // Probe on j_k_ff_5_q
  J_K_Flip_Flop j_k_ff_2 (
    .J(x), .clk(j_k_ff_1_qn), .K(x), .Q(j_k_ff_2_q), .Qn(j_k_ff_2_qn), .reset(or_1_out));  // open: preset
  // Probe on j_k_ff_4_q
  // Probe on j_k_ff_3_q
  J_K_Flip_Flop j_k_ff_3 (
    .J(x), .clk(j_k_ff_2_qn), .K(x), .Q(j_k_ff_3_q), .Qn(j_k_ff_3_qn), .reset(or_1_out));  // open: preset
  // Probe on j_k_ff_2_q
  // Probe on j_k_ff_1_q
  J_K_Flip_Flop j_k_ff_4 (
    .J(x), .clk(j_k_ff_3_qn), .K(x), .Q(j_k_ff_4_q), .Qn(j_k_ff_4_qn), .reset(or_1_out));  // open: preset
  J_K_Flip_Flop j_k_ff_5 (
    .J(x), .clk(j_k_ff_4_qn), .K(x), .Q(j_k_ff_5_q), .Qn(j_k_ff_5_qn), .reset(or_1_out));  // open: preset

  // Notes on the sheet:
  //   Contador assíncrono $decádico $crescente (5 bits)
endmodule

module dec_decresc_as (
  input  x,
  input  CLR
);

  wire and_1_out, CLK_out, j_k_ff_1_q, j_k_ff_2_q, j_k_ff_2_qn, j_k_ff_3_q, j_k_ff_4_q, j_k_ff_4_qn,
       j_k_ff_5_q, or_1_out;

  Clock CLK (.out(CLK_out));
  and and_1 (and_1_out, j_k_ff_1_q, j_k_ff_2_qn, j_k_ff_3_q, j_k_ff_4_qn, j_k_ff_5_q);
  J_K_Flip_Flop #(.Pre_Clr_Positions("BELOW_ABOVE")) j_k_ff_1 (
    .J(x), .clk(CLK_out), .K(x), .Q(j_k_ff_1_q), .preset(or_1_out));  // open: Qn, reset
  or or_1 (or_1_out, CLR, and_1_out);
  // Probe on j_k_ff_5_q
  J_K_Flip_Flop #(.Pre_Clr_Positions("BELOW_ABOVE")) j_k_ff_2 (
    .J(x), .clk(j_k_ff_1_q), .K(x), .Q(j_k_ff_2_q), .Qn(j_k_ff_2_qn), .preset(or_1_out));  // open: reset
  // Probe on j_k_ff_4_q
  // Probe on j_k_ff_3_q
  J_K_Flip_Flop #(.Pre_Clr_Positions("BELOW_ABOVE")) j_k_ff_3 (
    .J(x), .clk(j_k_ff_2_q), .K(x), .Q(j_k_ff_3_q), .preset(or_1_out));  // open: Qn, reset
  // Probe on j_k_ff_1_q
  // Probe on j_k_ff_2_q
  J_K_Flip_Flop #(.Pre_Clr_Positions("BELOW_ABOVE")) j_k_ff_4 (
    .J(x), .clk(j_k_ff_3_q), .K(x), .Q(j_k_ff_4_q), .Qn(j_k_ff_4_qn), .preset(or_1_out));  // open: reset
  J_K_Flip_Flop #(.Pre_Clr_Positions("BELOW_ABOVE")) j_k_ff_5 (
    .J(x), .clk(j_k_ff_4_q), .K(x), .Q(j_k_ff_5_q), .preset(or_1_out));  // open: Qn, reset

  // Notes on the sheet:
  //   Contador assíncrono $decádico $decrescente (5 bits)
endmodule

module sinc_mod7 (
  input  CLR,
  input  x
);

  wire and_1_out, and_2_out, and_3_out, and_4_out, and_5_out, and_6_out, and_7_out, CLK_out, not_1_out,
       or_1_out, or_2_out, t_ff_1_q, t_ff_1_qn, t_ff_2_q, t_ff_2_qn, t_ff_3_q, t_ff_3_qn, xor_1_out;

  Clock CLK (.out(CLK_out));
  and and_1 (and_1_out, x, t_ff_2_q, xor_1_out);
  T_Flip_Flop #(.Pre_Clr_Positions("BELOW_ABOVE")) t_ff_1 (
    .clk(CLK_out), .T(and_1_out), .Q(t_ff_1_q), .Qn(t_ff_1_qn), .reset(CLR));  // open: preset
  xor xor_1 (xor_1_out, t_ff_1_q, t_ff_3_q);
  // Probe on t_ff_1_q
  and and_2 (and_2_out, not_1_out, t_ff_2_q, t_ff_1_q, t_ff_3_qn);
  not not_1 (not_1_out, x);
  or or_1 (or_1_out, and_2_out, and_3_out, and_4_out);
  and and_3 (and_3_out, t_ff_1_qn, t_ff_3_q, x);
  T_Flip_Flop #(.Pre_Clr_Positions("BELOW_ABOVE")) t_ff_2 (
    .clk(CLK_out), .T(or_1_out), .Q(t_ff_2_q), .Qn(t_ff_2_qn), .reset(CLR));  // open: preset
  and and_4 (and_4_out, t_ff_1_q, t_ff_2_qn, t_ff_3_q, x);
  // Probe on t_ff_2_q
  or or_2 (or_2_out, and_6_out, and_5_out, and_7_out);
  and and_5 (and_5_out, t_ff_1_qn, t_ff_2_q, x);
  and and_6 (and_6_out, t_ff_1_qn, t_ff_2_qn, x);
  T_Flip_Flop #(.Pre_Clr_Positions("BELOW_ABOVE")) t_ff_3 (
    .clk(CLK_out), .T(or_2_out), .Q(t_ff_3_q), .Qn(t_ff_3_qn), .reset(CLR));  // open: preset
  and and_7 (and_7_out, t_ff_1_q, t_ff_2_qn, x);
  // Probe on t_ff_3_q

  // Notes on the sheet:
  //   Contador síncrono $módulo 7
endmodule
