// Logisim project Guia_14.circ as structural Verilog: 7 circuits, main circuit left_shift_a_v1
module left_shift_a_v1 (
  input  LD,
  input  CLR,
  output a,
  output b,
  output c,
  output d,
  output e,
  output f
);

  wire CLK_out;

  Clock CLK (.out(CLK_out));
  D_Flip_Flop d_ff_1 (.clk(CLK_out), .D(b), .Q(a), .reset(CLR));  // open: Qn, preset
  D_Flip_Flop d_ff_2 (.clk(CLK_out), .D(c), .Q(b), .reset(CLR));  // open: Qn, preset
  D_Flip_Flop d_ff_3 (.clk(CLK_out), .D(d), .Q(c), .reset(CLR));  // open: Qn, preset
  D_Flip_Flop d_ff_4 (.clk(CLK_out), .D(e), .Q(d), .reset(CLR));  // open: Qn, preset
  D_Flip_Flop d_ff_5 (.clk(CLK_out), .D(f), .Q(e), .reset(CLR));  // open: Qn, preset
  D_Flip_Flop d_ff_6 (.clk(CLK_out), .D(1'b0), .Q(f), .preset(LD), .reset(CLR));  // open: Qn
endmodule

module left_shift_a_v2 (
  input  CLR,
  input  LD,
  output a,
  output b,
  output c,
  output d,
  output e,
  output f
);

  wire CLK_out;

  Clock CLK (.out(CLK_out));
  D_Flip_Flop d_ff_1 (.clk(CLK_out), .D(b), .Q(a), .reset(CLR));  // open: Qn, preset
  D_Flip_Flop d_ff_2 (.clk(CLK_out), .D(c), .Q(b), .reset(CLR));  // open: Qn, preset
  D_Flip_Flop d_ff_3 (.clk(CLK_out), .D(d), .Q(c), .reset(CLR));  // open: Qn, preset
  D_Flip_Flop d_ff_4 (.clk(CLK_out), .D(e), .Q(d), .reset(CLR));  // open: Qn, preset
  D_Flip_Flop d_ff_5 (.clk(CLK_out), .D(f), .Q(e), .reset(CLR));  // open: Qn, preset
  D_Flip_Flop d_ff_6 (.clk(CLK_out), .D(LD), .Q(f), .reset(CLR));  // open: Qn, preset
endmodule

module left_shift_b_v1 (
  input  LD,
  input  CLR,
  output a,
  output b,
  output c,
  output d,
  output e,
  output f
);

  wire CLK_out;

  Clock CLK (.out(CLK_out));
  D_Flip_Flop d_ff_1 (.clk(CLK_out), .D(b), .Q(a), .preset(LD), .reset(CLR));  // open: Qn
  D_Flip_Flop d_ff_2 (.clk(CLK_out), .D(c), .Q(b), .preset(LD), .reset(CLR));  // open: Qn
  D_Flip_Flop d_ff_3 (.clk(CLK_out), .D(d), .Q(c), .preset(LD), .reset(CLR));  // open: Qn
  D_Flip_Flop d_ff_4 (.clk(CLK_out), .D(e), .Q(d), .preset(LD), .reset(CLR));  // open: Qn
  D_Flip_Flop d_ff_5 (.clk(CLK_out), .D(f), .Q(e), .preset(LD), .reset(CLR));  // open: Qn
  D_Flip_Flop d_ff_6 (.clk(CLK_out), .D(1'b0), .Q(f), .preset(LD), .reset(CLR));  // open: Qn
endmodule

module left_shift_b_v2 (
  input  CLR,
  input  LD,
  output a,
  output b,
  output c,
  output d,
  output e,
  output f
);

  wire CLK_out, or_1_out, or_2_out, or_3_out, or_4_out, or_5_out, or_6_out;

  Clock CLK (.out(CLK_out));
  or or_1 (or_1_out, b, LD);
  D_Flip_Flop d_ff_1 (.clk(CLK_out), .D(or_1_out), .Q(a), .reset(CLR));  // open: Qn, preset
  or or_2 (or_2_out, c, LD);
  D_Flip_Flop d_ff_2 (.clk(CLK_out), .D(or_2_out), .Q(b), .reset(CLR));  // open: Qn, preset
  D_Flip_Flop d_ff_3 (.clk(CLK_out), .D(or_3_out), .Q(c), .reset(CLR));  // open: Qn, preset
  or or_3 (or_3_out, d, LD);
  or or_4 (or_4_out, e, LD);
  D_Flip_Flop d_ff_4 (.clk(CLK_out), .D(or_4_out), .Q(d), .reset(CLR));  // open: Qn, preset
  or or_5 (or_5_out, f, LD);
  D_Flip_Flop d_ff_5 (.clk(CLK_out), .D(or_5_out), .Q(e), .reset(CLR));  // open: Qn, preset
  or or_6 (or_6_out, 1'b0, LD);
  D_Flip_Flop d_ff_6 (.clk(CLK_out), .D(or_6_out), .Q(f), .reset(CLR));  // open: Qn, preset
endmodule

module right_ring (
  input  \input ,
  input  CLR,
  output a,
  output b,
  output c,
  output d,
  output e,
  output f
);

  wire CLK_out, or_1_out;

  Clock CLK (.out(CLK_out));
  or or_1 (or_1_out, f, \input );
  D_Flip_Flop d_ff_1 (.clk(CLK_out), .D(or_1_out), .Q(a), .reset(CLR));  // open: Qn, preset
  D_Flip_Flop d_ff_2 (.clk(CLK_out), .D(a), .Q(b), .reset(CLR));  // open: Qn, preset
  D_Flip_Flop d_ff_3 (.clk(CLK_out), .D(b), .Q(c), .reset(CLR));  // open: Qn, preset
  D_Flip_Flop d_ff_4 (.clk(CLK_out), .D(c), .Q(d), .reset(CLR));  // open: Qn, preset
  D_Flip_Flop d_ff_5 (.clk(CLK_out), .D(d), .Q(e), .reset(CLR));  // open: Qn, preset
  D_Flip_Flop d_ff_6 (.clk(CLK_out), .D(e), .Q(f), .reset(CLR));  // open: Qn, preset
endmodule

module left_twisted_ring (
  input  \input ,
  input  CLR,
  output f,
  output e,
  output d,
  output c,
  output b,
  output a
);

  wire CLK_out, d_ff_6_qn, or_1_out;

  Clock CLK (.out(CLK_out));
  or or_1 (or_1_out, \input , d_ff_6_qn);
  D_Flip_Flop d_ff_1 (.clk(CLK_out), .D(or_1_out), .Q(a), .reset(CLR));  // open: Qn, preset
  D_Flip_Flop d_ff_2 (.clk(CLK_out), .D(a), .Q(b), .reset(CLR));  // open: Qn, preset
  D_Flip_Flop d_ff_3 (.clk(CLK_out), .D(b), .Q(c), .reset(CLR));  // open: Qn, preset
  D_Flip_Flop d_ff_4 (.clk(CLK_out), .D(c), .Q(d), .reset(CLR));  // open: Qn, preset
  D_Flip_Flop d_ff_5 (.clk(CLK_out), .D(d), .Q(e), .reset(CLR));  // open: Qn, preset
  D_Flip_Flop d_ff_6 (.clk(CLK_out), .D(e), .Q(f), .Qn(d_ff_6_qn), .reset(CLR));  // open: preset
endmodule

module paralell_serial (
  input  d5,
  input  d4,
  input  d3,
  input  d2,
  input  d1,
  input  d0,
  input  LD,
  input  CLR,
  output a,
  output b,
  output c,
  output d,
  output e,
  output f
);

  wire and_1_out, and_2_out, and_3_out, and_4_out, and_5_out, and_6_out, CLK_out;

  Clock CLK (.out(CLK_out));
  and and_1 (and_1_out, LD, d5);
  D_Flip_Flop d_ff_1 (.clk(CLK_out), .D(1'b0), .Q(a), .preset(and_1_out), .reset(CLR));  // open: Qn
  and and_2 (and_2_out, LD, d4);
  D_Flip_Flop d_ff_2 (.clk(CLK_out), .D(a), .Q(b), .preset(and_2_out), .reset(CLR));  // open: Qn
  and and_3 (and_3_out, LD, d3);
  D_Flip_Flop d_ff_3 (.clk(CLK_out), .D(b), .Q(c), .preset(and_3_out), .reset(CLR));  // open: Qn
  and and_4 (and_4_out, LD, d2);
  D_Flip_Flop d_ff_4 (.clk(CLK_out), .D(c), .Q(d), .preset(and_4_out), .reset(CLR));  // open: Qn
  and and_5 (and_5_out, LD, d1);
  D_Flip_Flop d_ff_5 (.clk(CLK_out), .D(d), .Q(e), .preset(and_5_out), .reset(CLR));  // open: Qn
  and and_6 (and_6_out, LD, d0);
  D_Flip_Flop d_ff_6 (.clk(CLK_out), .D(e), .Q(f), .preset(and_6_out), .reset(CLR));  // open: Qn
endmodule
