// Logisim project Guia_17.circ as structural Verilog: 5 circuits, main circuit q01_ffD
module q01_ffD (
  input  c,
  output a,
  output b
);

  wire and_1_out, and_2_out, and_3_out, and_4_out, CLK_out, or_1_out, or_2_out;

  Clock CLK (.out(CLK_out));
  or or_1 (or_1_out, and_1_out, and_2_out);
  and and_1 (and_1_out, a, ~c);  // AND_Gate
  and and_2 (and_2_out, b, c);
  D_Flip_Flop d_ff_1 (.clk(CLK_out), .D(or_1_out), .Q(a));  // open: Qn, preset, reset
  or or_2 (or_2_out, and_3_out, and_4_out);
  and and_3 (and_3_out, c, ~a);  // AND_Gate
  and and_4 (and_4_out, b, ~c);  // AND_Gate
  D_Flip_Flop d_ff_2 (.clk(CLK_out), .D(or_2_out), .Q(b));  // open: Qn, preset, reset
endmodule

module q02_ffJK_SR (
  input  c,
  output a,
  output b
);

  wire and_1_out, and_2_out, and_3_out, and_4_out, CLK_out;

  Clock CLK (.out(CLK_out));
  and and_1 (and_1_out, a, ~b, c);  // AND_Gate
  and and_2 (and_2_out, ~a, b, c);  // AND_Gate
  J_K_Flip_Flop j_k_ff_1 (.J(and_2_out), .clk(CLK_out), .K(and_1_out), .Q(a));  // open: Qn, preset, reset
  and and_3 (and_3_out, a, b, c);
  and and_4 (and_4_out, ~a, ~b, c);  // AND_Gate
  J_K_Flip_Flop j_k_ff_2 (.J(and_4_out), .clk(CLK_out), .K(and_3_out), .Q(b));  // open: Qn, preset, reset
endmodule

module q03_ffJK_T (
  input  c,
  output a,
  output b
);

  wire and_1_out, and_2_out, and_3_out, CLK_out, or_1_out, xor_1_out;

  Clock CLK (.out(CLK_out));
  and and_1 (and_1_out, xor_1_out, c);
  xor xor_1 (xor_1_out, a, b);
  J_K_Flip_Flop j_k_ff_1 (.J(and_1_out), .clk(CLK_out), .K(and_1_out), .Q(a));  // open: Qn, preset, reset
  and and_2 (and_2_out, a, b, c);
  or or_1 (or_1_out, and_2_out, and_3_out);
  and and_3 (and_3_out, ~a, ~b, c);  // AND_Gate
  J_K_Flip_Flop j_k_ff_2 (.J(or_1_out), .clk(CLK_out), .K(or_1_out), .Q(b));  // open: Qn, preset, reset
endmodule

module q04_contAS01 (
  output Q3,
  output Q2,
  output Q1
);

  wire CLK_out;

  Clock CLK (.out(CLK_out));
  T_Flip_Flop t_ff_1 (.clk(CLK_out), .T(1'b1), .Q(Q1));  // open: Qn, preset, reset
  T_Flip_Flop t_ff_2 (.clk(Q1), .T(1'b1), .Q(Q2));  // open: Qn, preset, reset
  T_Flip_Flop t_ff_3 (.clk(Q2), .T(1'b1), .Q(Q3));  // open: Qn, preset, reset
endmodule

module q05_contAS02 (
  output Q3,
  output Q2,
  output Q1
);

  wire CLK_out, t_ff_1_qn, t_ff_2_qn;

  Clock CLK (.out(CLK_out));
  T_Flip_Flop t_ff_1 (.clk(CLK_out), .T(1'b1), .Q(Q1), .Qn(t_ff_1_qn));  // open: preset, reset
  T_Flip_Flop t_ff_2 (.clk(t_ff_1_qn), .T(1'b1), .Q(Q2), .Qn(t_ff_2_qn));  // open: preset, reset
  T_Flip_Flop t_ff_3 (.clk(t_ff_2_qn), .T(1'b1), .Q(Q3));  // open: Qn, preset, reset
endmodule
