// Logisim project Decodificadores.circ as structural Verilog: 5 circuits, main circuit decodificador-alto
module decodificador_alto (
  input  e1,
  input  e2,
  output s3,
  output s2,
  output s1,
  output s0
);

  wire not_1_out, not_2_out;

  not not_1 (not_1_out, e2);
  not not_2 (not_2_out, e1);
  and and_1 (s3, not_1_out, not_2_out);
  and and_2 (s2, not_2_out, e2);
  and and_3 (s1, not_1_out, e1);
  and and_4 (s0, e2, e1);
endmodule

module decodificador_baixo (
  input  e1,
  input  e2,
  output s3,
  output s2,
  output s1,
  output s0
);

  wire not_1_out, not_2_out;

  not not_1 (not_1_out, e2);
  not not_2 (not_2_out, e1);
  nand nand_1 (s3, not_1_out, not_2_out);
  nand nand_2 (s2, not_2_out, e2);
  nand nand_3 (s1, not_1_out, e1);
  nand nand_4 (s0, e2, e1);
endmodule

module MUX2x1 (
  input  x,
  input  y,
  input  e,
  output s
);

  wire and_1_out, and_2_out, not_1_out;

  not not_1 (not_1_out, e);
  and and_1 (and_1_out, x, e);
  and and_2 (and_2_out, y, not_1_out);
  or or_1 (s, and_1_out, and_2_out);
endmodule

module MUX4x1 (
  input  e1,
  input  e0,
  input  x,
  input  y,
  input  v,
  input  w,
  output s
);

  wire and_1_out, and_2_out, and_3_out, and_4_out, not_1_out, not_2_out;

  not not_1 (not_1_out, e1);
  not not_2 (not_2_out, e0);
  and and_1 (and_1_out, not_2_out, not_1_out, x);
  and and_2 (and_2_out, e0, not_1_out, y);
  and and_3 (and_3_out, not_2_out, e1, v);
  and and_4 (and_4_out, e0, e1, w);
  or or_1 (s, and_1_out, and_2_out, and_3_out, and_4_out);
endmodule

module DEMUX1x4 (
  input  e1,
  input  e0,
  input  x,
  output s3,
  output s2,
  output s1,
  output s0
);

  wire not_1_out, not_2_out;

  not not_1 (not_1_out, e1);
  not not_2 (not_2_out, e0);
  and and_1 (s3, not_2_out, not_1_out, x);
  and and_2 (s2, e0, not_1_out, x);
  and and_3 (s1, not_2_out, e1, x);
  and and_4 (s0, e0, e1, x);
endmodule
