// Logisim project RAM.circ as structural Verilog: 6 circuits, main circuit 1x1_flip-flopD
// 1x1
module _1x1_flip_flopD (
  input  address,
  input  R_W,
  input  CLK,
  input  \input ,
  input  CLR,
  output \output 
);

  wire and_1_out, d_ff_1_q;

  and and_1 (and_1_out, address, R_W, CLK);
  D_Flip_Flop d_ff_1 (.clk(and_1_out), .D(\input ), .Q(d_ff_1_q), .reset(CLR));  // open: Qn, preset
  and and_2 (\output , address, d_ff_1_q);
endmodule

module _1x1 (
  input  R_W,
  input  address,
  input  CLK,
  input  CLR,
  input  \input ,
  output \output 
);

  _1x1_flip_flopD u_1x1_flip_flopd_1 (
    .R_W(R_W), .\input (\input ), .address(address), .\output (\output ), .CLR(CLR), .CLK(CLK));
endmodule

module _1x2 (
  input  R_W,
  input  address,
  input  CLK,
  input  CLR,
  input  [1:0] \input ,
  output [1:0] \output 
);

  _1x1_flip_flopD u_1x1_flip_flopd_1 (
    .R_W(R_W), .\input (\input [0]), .address(address), .\output (\output [0]), .CLR(CLR), .CLK(CLK));
  _1x1_flip_flopD u_1x1_flip_flopd_2 (
    .R_W(R_W), .\input (\input [1]), .address(address), .\output (\output [1]), .CLR(CLR), .CLK(CLK));
endmodule

module _1x4 (
  input  R_W,
  input  address,
  input  CLK,
  input  CLR,
  input  [3:0] \input ,
  output [3:0] \output 
);

  _1x2 u_1x2_1 (.R_W(R_W), .CLK(CLK), .CLR(CLR), .address(address), .\output (\output [1:0]), .\input (\input [1:0]));
  _1x2 u_1x2_2 (.R_W(R_W), .CLK(CLK), .CLR(CLR), .address(address), .\output (\output [3:2]), .\input (\input [3:2]));
endmodule

module _2x1 (
  input  R_W,
  input  address,
  input  CLK,
  input  CLR,
  input  \input ,
  output \output 
);

  wire demultiplexer_1_out0, demultiplexer_1_out1, n1x1_flip_flopd_1_output, n1x1_flip_flopd_2_output;

  _1x1_flip_flopD u_1x1_flip_flopd_1 (
    .R_W(R_W), .\input (\input ), .address(demultiplexer_1_out1), .\output (n1x1_flip_flopd_1_output),
    .CLR(CLR), .CLK(CLK));
  _1x1_flip_flopD u_1x1_flip_flopd_2 (
    .R_W(R_W), .\input (\input ), .address(demultiplexer_1_out0), .\output (n1x1_flip_flopd_2_output),
    .CLR(CLR), .CLK(CLK));
  Demultiplexer #(.enable("false")) demultiplexer_1 (
    .out0(demultiplexer_1_out0), .out1(demultiplexer_1_out1), .in(1'b1), .sel(address));
  Multiplexer #(.enable("false")) multiplexer_1 (
    .in0(n1x1_flip_flopd_2_output), .in1(n1x1_flip_flopd_1_output), .out(\output ), .sel(address));
endmodule

module _4x4 (
  input  [1:0] address,
  input  R_W,
  input  [3:0] \input ,
  input  CLK,
  input  CLR,
  output [3:0] \output 
);

  wire demultiplexer_1_out0, demultiplexer_1_out1, demultiplexer_1_out2, demultiplexer_1_out3;
  wire [3:0] n1x4_1_output, n1x4_2_output, n1x4_3_output, n1x4_4_output;

  Demultiplexer #(.select(2), .enable("false")) demultiplexer_1 (
    .out0(demultiplexer_1_out0), .out1(demultiplexer_1_out1), .out2(demultiplexer_1_out2),
    .out3(demultiplexer_1_out3), .in(1'b1), .sel(address));
  _1x4 u_1x4_1 (
    .R_W(R_W), .CLK(CLK), .CLR(CLR), .address(demultiplexer_1_out0), .\output (n1x4_1_output),
    .\input (\input ));
  _1x4 u_1x4_2 (
    .R_W(R_W), .CLK(CLK), .CLR(CLR), .address(demultiplexer_1_out1), .\output (n1x4_2_output),
    .\input (\input ));
  _1x4 u_1x4_3 (
    .R_W(R_W), .CLK(CLK), .CLR(CLR), .address(demultiplexer_1_out2), .\output (n1x4_3_output),
    .\input (\input ));
  _1x4 u_1x4_4 (
    .R_W(R_W), .CLK(CLK), .CLR(CLR), .address(demultiplexer_1_out3), .\output (n1x4_4_output),
    .\input (\input ));
  Multiplexer #(.select(2), .width(4), .enable("false")) multiplexer_1 (
    .in0(n1x4_1_output), .in1(n1x4_2_output), .in2(n1x4_3_output), .in3(n1x4_4_output), .out(\output ),
    .sel(address));
endmodule
