// Logisim project Somadores-Subtratores.circ as structural Verilog: 5 circuits, main circuit meia-soma
module meia_soma (
  input  x,
  input  y,
  output s0,
  output s1
);

  wire not_1_out, or_1_out;

  or or_1 (or_1_out, x, y);
  and and_1 (s1, x, y);
  and and_2 (s0, or_1_out, not_1_out);
  not not_1 (not_1_out, s1);

  // Notes on the sheet:
  //   s2
  //   s4
  //   s3
  //   (x+y).(x.y)'$=x'.y+x.y'$=XOR(x,y)
  //   x.y
endmodule

module meia_somaXOR (
  input  x,
  input  y,
  output s0,
  output s1
);

  xor xor_1 (s0, x, y);
  and and_1 (s1, x, y);

  // Notes on the sheet:
  //   XOR(x,y)
  //   x.y
endmodule

module soma_completa (
  input  vai_um,
  input  x,
  input  y,
  output s0,
  output s1
);

  wire and_1_out, and_2_out, xor_1_out;

  xor xor_1 (xor_1_out, x, y);
  and and_1 (and_1_out, x, y);
  xor xor_2 (s0, vai_um, xor_1_out);
  and and_2 (and_2_out, vai_um, xor_1_out);
  or or_1 (s1, and_2_out, and_1_out);
endmodule

module meia_diferenca (
  input  x,
  input  y,
  output s0,
  output s1
);

  wire not_1_out;

  xor xor_1 (s0, x, y);
  not not_1 (not_1_out, x);
  and and_1 (s1, not_1_out, y);

  // Notes on the sheet:
  //   XOR(x,y)
  //   x'.y
endmodule

module diferenca_completa (
  input  vem_um,
  input  x,
  input  y,
  output s0,
  output s1
);

  wire and_1_out, and_2_out, not_1_out, not_2_out, xor_1_out;

  not not_1 (not_1_out, x);
  not not_2 (not_2_out, xor_1_out);
  xor xor_1 (xor_1_out, x, y);
  and and_1 (and_1_out, not_1_out, y);
  xor xor_2 (s0, vem_um, xor_1_out);
  and and_2 (and_2_out, vem_um, not_2_out);
  or or_1 (s1, and_2_out, and_1_out);
endmodule
