// Logisim project Recuperacao_01.circ as structural Verilog: 5 circuits, main circuit q04_a
module q01_SoP (
  input  a,
  input  b,
  input  c,
  input  d,
  output s
);

  wire and_1_out, and_2_out, and_3_out, and_4_out, and_5_out, not_1_out, not_2_out, not_3_out, not_4_out;

  not not_1 (not_1_out, a);
  not not_2 (not_2_out, b);
  not not_3 (not_3_out, c);
  not not_4 (not_4_out, d);
  and and_1 (and_1_out, not_1_out, not_2_out, not_3_out);
  and and_2 (and_2_out, not_1_out, not_3_out, d);
  and and_3 (and_3_out, a, not_3_out, not_4_out);
  and and_4 (and_4_out, a, not_2_out, not_3_out);
  and and_5 (and_5_out, b, c, not_4_out);
  or or_1 (s, and_1_out, and_2_out, and_3_out, and_4_out, and_5_out);
endmodule

module q01_PoS (
  input  A,
  input  B,
  input  C,
  input  D,
  output S
);

  wire not_1_out, not_2_out, not_3_out, not_4_out, or_1_out, or_2_out, or_3_out, or_4_out, or_5_out;

  not not_1 (not_1_out, B);
  not not_2 (not_2_out, D);
  not not_3 (not_3_out, A);
  not not_4 (not_4_out, C);
  or or_1 (or_1_out, A, B, not_4_out);
  or or_2 (or_2_out, not_3_out, not_1_out, not_2_out);
  or or_3 (or_3_out, not_3_out, B, not_4_out);
  or or_4 (or_4_out, A, not_1_out, C, D);
  or or_5 (or_5_out, not_4_out, not_2_out);
  and and_1 (S, or_1_out, or_2_out, or_3_out, or_4_out, or_5_out);
endmodule

module q04_a (
  input  a,
  input  b,
  input  c,
  output s1,
  output s2
);

  wire nor_1_out, nor_2_out, nor_3_out, nor_4_out, not_1_out, not_2_out;

  not not_1 (not_1_out, a);
  nor nor_1 (nor_1_out, a, a);
  nor nor_2 (nor_2_out, not_1_out, b);
  nor nor_3 (nor_3_out, nor_1_out, b);
  not not_2 (not_2_out, nor_2_out);
  nor nor_4 (nor_4_out, nor_3_out, nor_3_out);
  nor nor_5 (s1, not_2_out, c);
  nor nor_6 (s2, nor_4_out, c);

  // Notes on the sheet:
  //   Expressão simplificada
  //   Expressão original
endmodule

module q04_b (
  input  a,
  input  b,
  output s1,
  output s2
);

  wire nand_1_out, nand_2_out, nand_3_out, nand_4_out;

  nand nand_1 (nand_1_out, a, a);
  nand nand_2 (nand_2_out, b, b);
  xor xor_1 (s1, a, b);
  nand nand_3 (nand_3_out, nand_1_out, b);
  nand nand_4 (nand_4_out, nand_2_out, a);
  nand nand_5 (s2, nand_3_out, nand_4_out);

  // Notes on the sheet:
  //   Expressão simplificada
  //   Expressão original
endmodule

module q04_c (
  input  a,
  input  b,
  input  c,
  output s
);

  wire multiplexer_1_out, multiplexer_2_out, not_1_out, not_2_out;

  not not_1 (not_1_out, a);
  Multiplexer #(.enable("false")) multiplexer_1 (.in0(not_1_out), .in1(b), .out(multiplexer_1_out), .sel(c));
  Multiplexer #(.enable("false")) multiplexer_2 (.in0(b), .in1(c), .out(multiplexer_2_out), .sel(a));
  Multiplexer #(.enable("false")) multiplexer_3 (
    .in0(multiplexer_2_out), .in1(multiplexer_1_out), .out(s), .sel(not_2_out));
  not not_2 (not_2_out, c);
endmodule
